// Logisim project SD_Group07.circ as structural Verilog: 3 circuits, main circuit main
module main (
  output [11:0] pc,
  output [11:0] r0,
  output [11:0] r1,
  output [11:0] r2,
  output [11:0] r3,
  output [11:0] r4,
  output [11:0] r5,
  output [11:0] r6,
  output [11:0] r7,
  output [3:0] OP,
  output [12:0] out_11,
  output halt
);

  wire and_1_out, clock_1_out, reset_out;
  wire [3:0] bit_extender_1_out;
  wire [11:0] program_counter_1_out_6, register_file_1_p4, register_file_1_p7, register_file_1_p8;

  Halt halt_1 (.instruction({OP, out_11[8:0]}), .clock(clock_1_out), .reset(reset_out), .halt(halt));
  Clock clock_1 (.out(clock_1_out));
  Button reset (.out(reset_out));
  and and_1 (and_1_out, ~halt, clock_1_out);  // AND_Gate
  program_counter program_counter_1 (
    .Branch_relative(1'b0), .Branch_absolute(1'b0), .C(and_1_out), .Reset(1'b0),
    .out_6(program_counter_1_out_6));  // open: Branch_value
  RAM #(.addrWidth(12), .dataWidth(13)) ram_1 (
    .addr(program_counter_1_out_6), .data({OP, out_11[8:0]}));  // open: sel, clk, ld, clr
  assign bit_extender_1_out = {{1{1'b1}}, out_11[2:0]};  // Bit_Extender bit_extender_1
  // register_file register_file_1: pin names not known; wires that end beside it: out_11[8:6], and_1_out, out_11[5:3], register_file_1_p4, 1'b1, 1'b0, register_file_1_p7, register_file_1_p8
  _12_bit_ALU u_12_bit_alu_1 (
    .ALU_code(bit_extender_1_out), .a(register_file_1_p7), .b(register_file_1_p8), .result(register_file_1_p4));  // open: overflow

  assign out_11[12:9] = OP;

  // Notes on the sheet:
  //   RD
  //   RS
  //   ALU Code
  //   current instruction
  //   clock signal
  //   reset button
  //   DO NOT CHANGE THE INPUTS AND OUTPUTS OF THIS CIRCUIT! Do not add/remove inputs or outputs. Do not even change their location or orientation.
endmodule

module Halt (
  input  [12:0] instruction,
  input  clock,
  input  reset,
  output halt
);

  wire and_1_out, comparator_1_eq, comparator_2_gt, counter_1_carry, or_1_out, or_2_out;
  wire [11:0] counter_1_q;

  Comparator #(.width(13), .mode("unsigned")) comparator_1 (
    .a(instruction), .b({13{1'b0}}), .eq(comparator_1_eq));  // open: gt, lt
  Counter #(.width(12), .max('hfff), .trigger("falling")) counter_1 (
    .Q(counter_1_q), .carry(counter_1_carry), .clk(clock), .clr(reset));  // open: load, D, count
  or or_1 (or_1_out, comparator_1_eq, counter_1_carry);
  Comparator #(.width(12), .mode("unsigned")) comparator_2 (
    .a(counter_1_q), .b({12{1'b0}}), .gt(comparator_2_gt));  // open: eq, lt
  or or_2 (or_2_out, halt, and_1_out);
  and and_1 (and_1_out, or_1_out, comparator_2_gt);
  Register #(.width(1)) register_1 (.D(or_2_out), .Q(halt), .clk(clock), .clr(reset));  // open: en

  // Notes on the sheet:
  //   halt becomes and stays asserted if the instruction is 0000 (not in the first clock cycle) or the end of the counter is reached (2^12)
endmodule

module program_counter (
  input  Branch_relative,
  input  Branch_absolute,
  input  [11:0] Branch_value,
  input  C,
  input  Reset,
  output [11:0] out_6
);

  wire and_1_out;
  wire [1:0] priority_encoder_1_out;
  wire [11:0] multiplexer_1_out, n12bit_cla_1_out_4, n12bit_cla_2_out_4;

  _12bit_CLA u_12bit_cla_1 (
    .in_1(Branch_value), .in_2(out_6), .in_3(1'b0), .out_4(n12bit_cla_1_out_4));  // open: Overflow
  and and_1 (and_1_out, ~Branch_relative, ~Branch_absolute);  // AND_Gate
  Priority_Encoder #(.select(2)) priority_encoder_1 (
    .in0(Branch_relative), .in1(Branch_absolute), .in2(and_1_out), .out(priority_encoder_1_out));  // open: in3, gs, en_out, en_in
  Multiplexer #(.select(2), .width(12), .enable("false")) multiplexer_1 (
    .in0(n12bit_cla_1_out_4), .in1(Branch_value), .in2(n12bit_cla_2_out_4), .out(multiplexer_1_out),
    .sel(priority_encoder_1_out));  // open: in3
  _12bit_register u_12bit_register_1 (.Input(multiplexer_1_out), .Reset(Reset), .Write(1'b1), .Clock(C), .out_5(out_6));
  _12bit_CLA u_12bit_cla_2 (.in_1(out_6), .in_2(12'h1), .in_3(1'b0), .out_4(n12bit_cla_2_out_4));  // open: Overflow
endmodule
